// Logisim project Decoder.circ as structural Verilog: 1 circuit, main circuit main
module main (
);

  wire and_1_out, and_2_out, and_3_out, and_4_out, button_1_out, button_2_out, not_1_out, not_2_out,
       not_3_out, not_4_out;

  Button button_1 (.out(button_1_out));
  not not_1 (not_1_out, button_1_out);
  not not_2 (not_2_out, button_1_out);
  not not_3 (not_3_out, button_2_out);
  not not_4 (not_4_out, button_2_out);
  Button button_2 (.out(button_2_out));
  and and_1 (and_1_out, not_1_out, not_3_out);
  and and_2 (and_2_out, not_2_out, button_2_out);
  and and_3 (and_3_out, button_1_out, not_4_out);
  and and_4 (and_4_out, button_1_out, button_2_out);
  LED led_1 (.in(and_1_out));
  LED led_2 (.in(and_2_out));
  LED led_3 (.in(and_3_out));
  LED led_4 (.in(and_4_out));

  // Notes on the sheet:
  //   1
  //   2
endmodule
