// Logisim project Multiplexer.circ as structural Verilog: 1 circuit, main circuit main
module main (
);

  wire and_1_out, and_2_out, and_3_out, and_4_out, and_5_out, and_6_out, and_7_out, and_8_out, button_1_out,
       button_2_out, not_1_out, not_2_out, not_3_out, not_4_out, or_1_out, or_2_out, or_3_out;

  Button button_1 (.out(button_1_out));
  not not_1 (not_1_out, button_1_out);
  not not_2 (not_2_out, button_1_out);
  not not_3 (not_3_out, button_2_out);
  not not_4 (not_4_out, button_2_out);
  Button button_2 (.out(button_2_out));
  and and_1 (and_1_out, not_1_out, not_3_out);
  and and_2 (and_2_out, not_2_out, button_2_out);
  and and_3 (and_3_out, button_1_out, not_4_out);
  and and_4 (and_4_out, button_1_out, button_2_out);
  and and_5 (and_5_out, and_1_out, 1'b1);
  and and_6 (and_6_out, and_2_out, 1'b0);
  and and_7 (and_7_out, and_3_out, 1'b1);
  and and_8 (and_8_out, and_4_out, 1'b1);
  or or_1 (or_1_out, and_5_out, and_6_out);
  or or_2 (or_2_out, and_7_out, and_8_out);
  or or_3 (or_3_out, or_1_out, or_2_out);

  // Notes on the sheet:
  //   2
endmodule
